// Logisim project Prog__012.circ as structural Verilog: 3 circuits, main circuit mul
module main (
  input  [3:0] a,
  input  [3:0] b,
  input  [3:0] a_2,
  input  [3:0] b_2,
  output [7:0] mul,
  output [7:0] out_6
);

  wire ck;
  wire [3:0] mul_1_cycle;
  wire [7:0] bit_extender_1_out, bit_extender_2_out;

  Clock u_ck (.out(ck));
  mul mul_1 (.mltplcnd(a), .mltplr(b), .ck(ck), .mul(mul), .cycle(mul_1_cycle));
  assign bit_extender_1_out = {{4{a_2[3]}}, a_2};  // Bit_Extender bit_extender_1
  assign bit_extender_2_out = {{4{b_2[3]}}, b_2};  // Bit_Extender bit_extender_2
  Hex_Digit_Display hex_digit_display_1 (.value(mul_1_cycle));  // open: dp
  Multiplier multiplier_1 (.a(bit_extender_1_out), .b(bit_extender_2_out), .out(out_6));  // open: cin, cout

  // Notes on the sheet:
  //   SIGNAL
  //   MULTIPLIER
endmodule

module mul (
  input  ck,
  input  [3:0] mltplcnd,
  input  [3:0] mltplr,
  output [7:0] mul,
  output [3:0] cycle
);

  wire alu4b_1_cout, comparator_1_eq, \end , lsb, start;
  wire [3:0] app, bit_extender_2_out, multiplexer_1_out, res, temp;
  wire [7:0] bit_extender_1_out, bit_extender_3_out, multiplexer_2_out, multiplexer_3_out, shifter_1_out;
  wire [7:4] prdct;
  wire [7:7] and_1_out;

  Counter #(.width(4), .max('hf)) counter_1 (.count(ck), .Q(cycle), .clk(ck), .clr(\end ));  // open: load, D, carry
  Comparator #(.width(4)) comparator_1 (.a(cycle), .b(4'b0000), .eq(comparator_1_eq));  // open: gt, lt
  Comparator #(.width(4)) comparator_2 (.a(cycle), .b(4'b0100), .eq(\end ));  // open: gt, lt
  not not_1 (start, comparator_1_eq);
  assign bit_extender_1_out = {{4{1'b0}}, mltplr};  // Bit_Extender bit_extender_1
  Multiplexer #(.width(4)) multiplexer_1 (
    .in0(mltplcnd), .in1(multiplexer_1_out), .out(multiplexer_1_out), .sel(start));  // open: en
  Multiplexer #(.select(2), .width(8)) multiplexer_2 (
    .in0(bit_extender_1_out), .in1({res, mltplr}), .in2({prdct, app}), .in3({res, app}),
    .out(multiplexer_2_out), .sel({start, lsb}));  // open: en
  ALU4b alu4b_1 (.a(multiplexer_1_out), .b(temp), .opcode(2'b10), .res(res), .cout(alu4b_1_cout));  // open: sign, zero
  Shifter #(.shift("lr")) shifter_1 (.in(multiplexer_2_out), .\dist (3'b001), .out(shifter_1_out));
  and and_1 (and_1_out[7], lsb, alu4b_1_cout);
  Register register_1 (.D({and_1_out[7], shifter_1_out[6:0]}), .Q({prdct, app}), .clk(ck));  // open: en, clr
  assign bit_extender_2_out = {{3{start}}, start};  // Bit_Extender bit_extender_2
  assign bit_extender_3_out = {{4{1'b0}}, mltplr};  // Bit_Extender bit_extender_3
  assign temp = prdct & bit_extender_2_out;  // AND_Gate and_2, 4 bits wide
  Multiplexer #(.width(8)) multiplexer_3 (
    .in0(bit_extender_3_out), .in1({prdct, app}), .out(multiplexer_3_out), .sel(start));  // open: en
  BitSelector bitselector_1 (.in(multiplexer_3_out), .out(lsb), .sel(3'b000));
  Multiplexer #(.width(8)) multiplexer_4 (.in0(mul), .in1({prdct, app}), .out(mul), .sel(\end ));  // open: en

  // Other names for the same wires on the sheet: prdct[3:0] = app

  // Notes on the sheet:
  //   INPUT
  //   CYCLE
  //   CIRCUIT
  //   OUTPUT
endmodule

module ALU4b (
  input  [1:0] opcode,
  input  [3:0] a,
  input  [3:0] b,
  output [3:0] res,
  output sign,
  output zero,
  output cout
);

  wire sub;
  wire [3:0] \and , bit_extender_1_out, op, \or , xor_1_out;

  and and_1 (sub, opcode[0], opcode[1]);
  assign \and  = a & b;  // AND_Gate and_2, 4 bits wide
  assign \or  = a | b;  // OR_Gate or_1, 4 bits wide
  assign xor_1_out = b ^ bit_extender_1_out;  // XOR_Gate xor_1, 4 bits wide
  assign bit_extender_1_out = {{3{sub}}, sub};  // Bit_Extender bit_extender_1
  Adder #(.width(4)) adder_1 (.a(a), .b(xor_1_out), .out(op), .cin(sub), .cout(cout));
  Multiplexer #(.select(2), .width(4)) multiplexer_1 (
    .in0(\and ), .in1(\or ), .in2(op), .in3(op), .out(res), .sel(opcode));  // open: en
  BitSelector #(.width(4)) bitselector_1 (.in(res), .out(sign), .sel(2'b11));
  Comparator #(.width(4)) comparator_1 (.a(res), .b(4'b0000), .eq(zero));  // open: gt, lt

  // Other names for the same wires on the sheet: oc[1:0] = opcode

  // Notes on the sheet:
  //   INPUT
  //   CIRCUIT / OUTPUT
endmodule
