// Logisim project Prog__017.circ as structural Verilog: 4 circuits, main circuit main
module main (
  input  en,
  input  Ta,
  input  rst,
  input  Tb,
  input  Ta_2,
  input  Tb_2
);

  wire ck, gr, loopgr, loopor, looprg, loopro, \or , or_1_out, or_2_out, or_4_out, or_5_out, rg, ro;
  wire [3:0] and_1_out, and_2_out, and_3_out, and_4_out, bit_extender_1_out, bit_extender_2_out,
       bit_extender_3_out, bit_extender_4_out, temp, tempgr, tempor, temprg, tempro;

  Clock u_ck (.out(ck));
  ctrlTemp ctrltemp_1 (
    .Ta(Ta_2), .Tb(Tb_2), .timegr(4'b0101), .timeor(4'b0010), .timerg(4'b0101), .timero(4'b0010), .ck(ck),
    .en(en), .rst(rst), .gr(gr), .tempgr(tempgr), .\or (\or ), .tempor(tempor), .rg(rg), .temprg(temprg),
    .ro(ro), .tempro(tempro));
  ctrl ctrl_1 (.Ta(Ta), .Tb(Tb), .ck(ck), .en(en), .rst(rst), .gr(loopgr), .\or (loopor), .rg(looprg), .ro(loopro));
  LED led_1 (.in(loopgr));
  LED led_2 (.in(loopor));
  or or_1 (or_1_out, looprg, loopro);
  LED led_3 (.in(or_1_out));
  LED led_4 (.in(looprg));
  LED led_5 (.in(loopro));
  LED led_6 (.in(or_2_out));
  or or_2 (or_2_out, loopgr, loopor);
  assign and_1_out = tempgr & bit_extender_1_out;  // AND_Gate and_1, 4 bits wide
  assign bit_extender_1_out = {{3{gr}}, gr};  // Bit_Extender bit_extender_1
  assign and_2_out = tempor & bit_extender_2_out;  // AND_Gate and_2, 4 bits wide
  assign bit_extender_2_out = {{3{\or }}, \or };  // Bit_Extender bit_extender_2
  assign and_3_out = temprg & bit_extender_3_out;  // AND_Gate and_3, 4 bits wide
  assign bit_extender_3_out = {{3{rg}}, rg};  // Bit_Extender bit_extender_3
  assign and_4_out = tempro & bit_extender_4_out;  // AND_Gate and_4, 4 bits wide
  assign bit_extender_4_out = {{3{ro}}, ro};  // Bit_Extender bit_extender_4
  assign temp = and_1_out | and_2_out | and_3_out | and_4_out;  // OR_Gate or_3, 4 bits wide
  LED led_7 (.in(gr));
  LED led_8 (.in(\or ));
  LED led_9 (.in(or_4_out));
  or or_4 (or_4_out, rg, ro);
  LED led_10 (.in(rg));
  LED led_11 (.in(ro));
  LED led_12 (.in(or_5_out));
  or or_5 (or_5_out, gr, \or );
  Hex_Digit_Display hex_digit_display_1 (.value(temp));  // open: dp

  // Notes on the sheet:
  //   SIGNAL
  //   MOORE FSM
  //   MOORE FSM TEMP
  //   TRAFFIC LIGHT
  //   TRAFFIC LIGHT TEMP
endmodule

// control
module ctrl (
  input  ck,
  input  en,
  input  rst,
  input  Ta,
  input  Tb,
  output gr,
  output \or ,
  output rg,
  output ro
);

  wire and_1_out, and_2_out, and_3_out, and_4_out, ns0, ns1, nTa, nTb, or_1_out, or_2_out, s0, s1;

  not not_1 (nTa, Ta);
  not not_2 (nTb, Tb);
  and and_1 (and_1_out, ns1, s0);
  or or_1 (or_1_out, and_1_out, and_2_out);
  and and_2 (and_2_out, s1, ns0);
  and and_3 (and_3_out, ns1, ns0, nTb);
  or or_2 (or_2_out, and_3_out, and_4_out);
  and and_4 (and_4_out, s1, ns0, nTa);
  D_Flip_Flop d_ff_1 (.clk(ck), .D(or_1_out), .Q(s1), .Qn(ns1), .en(en), .reset(rst));  // open: preset
  D_Flip_Flop d_ff_2 (.clk(ck), .D(or_2_out), .Q(s0), .Qn(ns0), .en(en), .reset(rst));  // open: preset
  and and_5 (gr, ns1, ns0);
  and and_6 (\or , ns1, s0);
  and and_7 (rg, s1, ns0);
  and and_8 (ro, s1, s0);

  // Notes on the sheet:
  //   INPUT
  //   CIRCUIT
  //   OUTPUT
endmodule

module ctrlTemp (
  input  ck,
  input  en,
  input  rst,
  input  [3:0] timegr,
  input  [3:0] timeor,
  input  [3:0] timerg,
  input  [3:0] timero,
  input  Ta,
  input  Tb,
  output gr,
  output [3:0] tempgr,
  output \or ,
  output [3:0] tempor,
  output rg,
  output [3:0] temprg,
  output ro,
  output [3:0] tempro
);

  wire and_1_out, and_2_out, and_3_out, and_4_out, engr, enor, enrg, enro, ns0, ns1, nTa, nTb, or_3_out,
       or_4_out, or_5_out, or_6_out, s0, s1;
  wire [1:0] multiplexer_3_out, multiplexer_4_out, or_1_out, or_2_out;

  not not_1 (nTa, Ta);
  not not_2 (nTb, Tb);
  Multiplexer #(.select(2)) multiplexer_1 (
    .in0(enor), .in1(enrg), .in2(enro), .in3(engr), .out(or_1_out[1]), .sel({s1, s0}));  // open: en
  and and_1 (and_1_out, ns1, s0);
  and and_2 (and_2_out, s1, ns0);
  Multiplexer #(.select(2)) multiplexer_2 (
    .in0(enor), .in1(enrg), .in2(enro), .in3(engr), .out(or_2_out[1]), .sel({s1, s0}));  // open: en
  and and_3 (and_3_out, ns1, ns0, nTb);
  and and_4 (and_4_out, s1, ns0, nTa);
  Multiplexer #(.select(2), .width(2)) multiplexer_3 (
    .in0(2'b00), .in1(2'b00), .in2(2'b10), .in3(2'b01), .out(multiplexer_3_out), .sel(or_1_out));  // open: en
  or or_1 (or_1_out[0], and_1_out, and_2_out);
  Multiplexer #(.select(2), .width(2)) multiplexer_4 (
    .in0(2'b00), .in1(2'b00), .in2(2'b10), .in3(2'b01), .out(multiplexer_4_out), .sel(or_2_out));  // open: en
  or or_2 (or_2_out[0], and_3_out, and_4_out);
  S_R_Flip_Flop s_r_ff_1 (
    .S(multiplexer_3_out[0]), .clk(ck), .R(multiplexer_3_out[1]), .Q(s1), .Qn(ns1), .reset(rst), .en(en));  // open: preset
  S_R_Flip_Flop s_r_ff_2 (
    .S(multiplexer_4_out[0]), .clk(ck), .R(multiplexer_4_out[1]), .Q(s0), .Qn(ns0), .reset(rst), .en(en));  // open: preset
  and and_5 (gr, ns1, ns0);
  and and_6 (\or , ns1, s0);
  and and_7 (rg, s1, ns0);
  and and_8 (ro, s1, s0);
  timer timer_1 (.\time (timegr), .ck(ck), .en(gr), .rst(or_3_out), .out(enor), .temp(tempgr));
  or or_3 (or_3_out, rst, \or );
  timer timer_2 (.\time (timeor), .ck(ck), .en(\or ), .rst(or_4_out), .out(enrg), .temp(tempor));
  or or_4 (or_4_out, rst, rg);
  timer timer_3 (.\time (timerg), .ck(ck), .en(rg), .rst(or_5_out), .out(enro), .temp(temprg));
  or or_5 (or_5_out, rst, ro);
  timer timer_4 (.\time (timero), .ck(ck), .en(ro), .rst(or_6_out), .out(engr), .temp(tempro));
  or or_6 (or_6_out, rst, gr);

  // Other names for the same wires on the sheet: rstro = gr; tongr = gr; rstgr = \or ; tonor = \or ; rstor = rg;
  //   tonrg = rg; rstrg = ro; tonro = ro

  // Notes on the sheet:
  //   INPUT
  //   CIRCUIT / OUTPUT
endmodule

module timer (
  input  ck,
  input  en,
  input  rst,
  input  [3:0] \time ,
  output out,
  output [3:0] temp
);

  wire and_1_out, and_2_out, comparator_1_eq;

  Counter #(.width(4), .max('hf)) counter_1 (
    .count(and_1_out), .Q(temp), .clk(and_1_out), .clr(rst));  // open: load, D, carry
  and and_1 (and_1_out, ck, en);
  Comparator #(.width(4)) comparator_1 (.a(temp), .b(\time ), .eq(comparator_1_eq));  // open: gt, lt
  or or_1 (out, comparator_1_eq, and_2_out);
  and and_2 (and_2_out, ~rst, out);  // AND_Gate

  // Notes on the sheet:
  //   INPUT
  //   CIRCUIT / OUTPUT
endmodule
