// Logisim project Prog__018.circ as structural Verilog: 4 circuits, main circuit main
module main (
  input  i,
  input  en,
  input  rst
);

  wire a, a7a, a7b, a7c, a7d, a7e, a7f, a7g, a7p, aclr, b, b7a, b7b, b7c, b7d, b7e, b7f, b7g, b7p, bclr, ck,
       comparator_1_eq, comparator_2_eq;
  wire [3:0] acnt, bcnt;

  Clock u_ck (.out(ck));
  findSeq findseq_1 (.i(i), .ck(ck), .en(en), .rst(rst), .a(a), .b(b));
  Counter #(.width(4), .max('hf)) counter_1 (.count(a), .Q(acnt), .clk(ck), .clr(aclr));  // open: load, D, carry
  Comparator #(.width(4)) comparator_1 (.a(acnt), .b(4'b1010), .eq(comparator_1_eq));  // open: gt, lt
  or or_1 (aclr, comparator_1_eq, rst);
  Counter #(.width(4), .max('hf)) counter_2 (.count(b), .Q(bcnt), .clk(ck), .clr(bclr));  // open: load, D, carry
  Comparator #(.width(4)) comparator_2 (.a(bcnt), .b(4'b1010), .eq(comparator_2_eq));  // open: gt, lt
  or or_2 (bclr, comparator_2_eq, rst);
  conv7Seg conv7seg_1 (.num(acnt), .a(a7a), .b(a7b), .c(a7c), .d(a7d), .e(a7e), .f(a7f), .g(a7g), .p(a7p));
  conv7Seg conv7seg_2 (.num(bcnt), .a(b7a), .b(b7b), .c(b7c), .d(b7d), .e(b7e), .f(b7f), .g(b7g), .p(b7p));
  _7_Segment_Display u_7_segment_display_1 (.g(a7g), .f(a7f), .a(a7a), .b(a7b), .e(a7e), .d(a7d), .c(a7c), .dp(a7p));
  _7_Segment_Display u_7_segment_display_2 (.g(b7g), .f(b7f), .a(b7a), .b(b7b), .e(b7e), .d(b7d), .c(b7c), .dp(b7p));

  // Notes on the sheet:
  //   SIGNAL
  //   MOORE FSM
  //   FINDER SEQUENCE A
  //   FINDER SEQUENCE B
endmodule

// seqBit
module findSeq (
  input  ck,
  input  en,
  input  rst,
  input  i,
  output a,
  output b
);

  wire and_1_out, and_2_out, and_3_out, and_4_out, and_5_out, and_6_out, and_7_out, and_8_out, and_9_out, ni,
       ns0, ns1, ns2, or_1_out, or_2_out, or_3_out, s0, s1, s2;

  not not_1 (ni, i);
  and and_1 (and_1_out, s1, i);
  or or_1 (or_1_out, and_1_out, and_2_out);
  and and_2 (and_2_out, s2, s0);
  and and_3 (and_3_out, ns2, s1, ns0, ni);
  and and_4 (and_4_out, ns2, ns1, s0, i);
  or or_2 (or_2_out, and_3_out, and_4_out, and_5_out, and_6_out);
  and and_5 (and_5_out, s2, ns1, ns0, i);
  and and_6 (and_6_out, s2, s0, ni);
  and and_7 (and_7_out, ns2, ns0, i);
  and and_8 (and_8_out, ns2, s1, ns0);
  or or_3 (or_3_out, and_7_out, and_8_out, and_9_out);
  and and_9 (and_9_out, s2, s0, i);
  D_Flip_Flop d_ff_1 (.clk(ck), .D(or_1_out), .Q(s2), .Qn(ns2), .en(en), .reset(rst));  // open: preset
  D_Flip_Flop d_ff_2 (.clk(ck), .D(or_2_out), .Q(s1), .Qn(ns1), .en(en), .reset(rst));  // open: preset
  D_Flip_Flop d_ff_3 (.clk(ck), .D(or_3_out), .Q(s0), .Qn(ns0), .en(en), .reset(rst));  // open: preset
  and and_10 (a, s2, ns1, ns0);
  and and_11 (b, s2, s1, ns0);

  // Notes on the sheet:
  //   INPUT
  //   CIRCUIT
  //   OUTPUT
endmodule

// conversion
module conv7Seg (
  input  [3:0] num,
  output a,
  output b,
  output c,
  output d,
  output e,
  output f,
  output g,
  output p
);

  wire decoder_1_out0, decoder_1_out1, decoder_1_out2, decoder_1_out3, decoder_1_out4, decoder_1_out5,
       decoder_1_out6, decoder_1_out7, decoder_1_out8, decoder_1_out9, decoder_1_out10;

  Decoder #(.select(4)) decoder_1 (
    .out0(decoder_1_out0), .out1(decoder_1_out1), .out2(decoder_1_out2), .out3(decoder_1_out3),
    .out4(decoder_1_out4), .out5(decoder_1_out5), .out6(decoder_1_out6), .out7(decoder_1_out7),
    .out8(decoder_1_out8), .out9(decoder_1_out9), .out10(decoder_1_out10), .sel(num));  // open: out11, out12, out13, out14, out15, en
  segment segment_1 (
    ._0(decoder_1_out0), ._1(decoder_1_out1), ._2(decoder_1_out2), ._3(decoder_1_out3), ._4(decoder_1_out4),
    ._5(decoder_1_out5), ._6(decoder_1_out6), ._7(decoder_1_out7), ._8(decoder_1_out8), ._9(decoder_1_out9),
    .p(decoder_1_out10), .a(a), .b(b), .c(c), .d(d), .e(e), .f(f), .g(g), .p_2(p));

  // Notes on the sheet:
  //   INPUT
  //   CIRCUIT / OUTPUT
endmodule

module segment (
  input  _0,
  input  _1,
  input  _2,
  input  _3,
  input  _4,
  input  _5,
  input  _6,
  input  _7,
  input  _8,
  input  _9,
  input  p,
  output a,
  output b,
  output c,
  output d,
  output e,
  output f,
  output g,
  output p_2
);

  or or_1 (a, _0, _2, _3, _5, _6, _7, _8, _9);
  or or_2 (d, _0, _2, _3, _5, _6, _8, _9);
  or or_3 (b, _0, _1, _2, _3, _4, _7, _8, _9);
  or or_4 (e, _0, _2, _6, _8);
  or or_5 (c, _0, _1, _3, _4, _5, _6, _7, _8, _9);
  or or_6 (f, _0, _4, _5, _6, _8, _9);
  or or_7 (g, _2, _3, _4, _5, _6, _8, _9);

  assign p_2 = p;

  // Notes on the sheet:
  //   INPUT
  //   CIRCUIT / OUTPUT
endmodule
